# Fritzing sketch OwlWeather (saved by Fritzing 0.9.3b)

parts:
  WeMos_D1_Mini1 = WeMos D1 Mini
  Part1 = 16-Channel 12-bit PWM Servo Driver - I2C [part_number=815]
  J2 = Basic Servo
  J3 = Basic Servo
  J4 = Basic Servo
  J5 = Basic Servo
  Part2 = Adafruit AMG8833 8x8 GRID EYE

nets:
  VCC: WeMos_D1_Mini1.3V3, Part1.5.0V, J2.vcc, J3.vcc, J4.vcc, J5.vcc
  N1: WeMos_D1_Mini1.5V, Part1.PWRIN
  N2: WeMos_D1_Mini1.D3, Part1.SCL, Part2.SCL
  N3: WeMos_D1_Mini1.D4, Part1.VCC, Part1.SDA, Part2.SDA
  GND: WeMos_D1_Mini1.G, Part1.GND, Part1.OE, J2.gnd, J3.gnd, J4.gnd, J5.gnd
  N4: Part1.PWM3, J5.pulse
  N5: Part1.PWM2, J4.pulse
  N6: Part1.PWM1, J3.pulse
  N7: Part1.PWM0, J2.pulse

custom parts:
  16-Channel 12-bit PWM Servo Driver - I2C: You want to make a cool robot, maybe a hexapod walker, or maybe just a piece of art with a lot of moving parts. Or maybe you want to drive a lot of LEDs with precise PWM output. Using only two pins, control 16 free-running PWM outputs! You can even chain up 62 breakouts to control up to 992 PWM outputs.
